# Fritzing sketch wemos-d1-mini (saved by Fritzing 0.9.10b)
breadboards: 1

parts:
  LCD1 = LCD screen
  RE1 = KY-040-AZ
  LCM1602_IIC2 = generic_ic_dip_22_300mil.fzp [part_number="LCM1602 IIC" chip_label="LCM1602 IIC"]
  ZS-042_RTC1 = ZS-042 RTC Module
  WeMos_D1_Mini2 = WeMos D1 Mini

nets:
  N1: LCD1.VSS, LCM1602_IIC2.connector0
  N2: LCD1.VDD, LCM1602_IIC2.connector1
  N3: LCD1.V0, LCM1602_IIC2.connector2
  N4: LCD1.RS, LCM1602_IIC2.connector3
  N5: LCD1.R/W, LCM1602_IIC2.connector4
  N6: LCD1.E, LCM1602_IIC2.connector5
  N7: LCD1.DB0, LCM1602_IIC2.connector6
  N8: LCD1.DB1, LCM1602_IIC2.connector7
  N9: LCD1.DB2, LCM1602_IIC2.connector8
  N10: LCD1.DB3, LCM1602_IIC2.connector9
  N11: LCD1.DB4, LCM1602_IIC2.connector10
  N12: LCD1.DB5, LCM1602_IIC2.connector11
  N13: LCD1.DB6, LCM1602_IIC2.connector12
  N14: LCD1.DB7, LCM1602_IIC2.connector13
  N15: LCD1.LED+, LCM1602_IIC2.connector14
  N16: LCD1.LED-, LCM1602_IIC2.connector15
  N17: RE1.connector0, LCM1602_IIC2.connector16, ZS-042_RTC1.GND, WeMos_D1_Mini2.G
  VCC: RE1.connector1, LCM1602_IIC2.connector17, ZS-042_RTC1.VCC, WeMos_D1_Mini2.3V3
  N18: RE1.connector2, WeMos_D1_Mini2.D7
  N19: RE1.connector3, WeMos_D1_Mini2.D6
  N20: RE1.connector4, WeMos_D1_Mini2.D5
  N21: LCM1602_IIC2.connector18, ZS-042_RTC1.SDA
  N22: LCM1602_IIC2.connector19, ZS-042_RTC1.SCL
